// Logisim project custom_seven_segment_display.circ as structural Verilog: 2 circuits, main circuit Main Circuit
module _4x7_Decoder (
  input  A,
  input  B,
  input  C,
  input  D,
  output out_5,
  output out_6,
  output out_7,
  output out_8,
  output out_9,
  output out_10,
  output out_11
);

  wire A_prime_B_out, A_prime_C_out, A_prime_out, AD_prime_out, B_prime_D_prime_out, B_prime_out, BC_out,
       BC_prime_out, C_prime_D_prime_out, C_prime_out, CD_out, D_prime_out;

  not A_prime (A_prime_out, A);
  not B_prime (B_prime_out, B);
  not C_prime (C_prime_out, C);
  not D_prime (D_prime_out, D);
  and B_prime_D_prime (B_prime_D_prime_out, B_prime_out, D_prime_out);
  and A_prime_B (A_prime_B_out, A_prime_out, B);
  and BC (BC_out, B, C);
  and C_prime_D_prime (C_prime_D_prime_out, C_prime_out, D_prime_out);
  and CD (CD_out, C, D);
  and A_prime_C (A_prime_C_out, A_prime_out, C);
  and BC_prime (BC_prime_out, B, C_prime_out);
  and AD_prime (AD_prime_out, A, D_prime_out);
  or u_a (out_5, B_prime_D_prime_out, C);
  or u_b (out_6, C_prime_out, B_prime_out, A);
  or u_c (out_7, C_prime_out, A_prime_B_out, D);
  or u_d (out_8, BC_out, B_prime_D_prime_out);
  or e (out_9, BC_out, B_prime_D_prime_out);
  or f (out_10, C_prime_D_prime_out, A_prime_B_out, CD_out);
  or g (out_11, A_prime_C_out, BC_prime_out, AD_prime_out);

  // Notes on the sheet:
  //   4x7 Decoder
endmodule

module Main_Circuit (
);

  wire a_out, A_prime_BC_out, AB_prime_C_prime_out, AB_prime_out, ABCD_prime_out, AC_prime_out, b_out,
       B_prime_C_prime_D_out, c_out, C_prime_D_prime_out, CD_out, clock_out, d_out, Da_q, Da_qn, Db_q, Db_qn,
       Dc_q, Dc_qn, Dd_q, Dd_qn, n4x7_decoder_1_out_5, n4x7_decoder_1_out_6, n4x7_decoder_1_out_7,
       n4x7_decoder_1_out_8, n4x7_decoder_1_out_9, n4x7_decoder_1_out_10, n4x7_decoder_1_out_11;

  and AC_prime (AC_prime_out, Da_q, Dc_qn);
  and CD (CD_out, Dc_q, Dd_q);
  and A_prime_BC (A_prime_BC_out, Da_qn, Db_q, Dc_q);
  and B_prime_C_prime_D (B_prime_C_prime_D_out, Db_qn, Dc_qn, Dd_qn);
  and AB_prime (AB_prime_out, Da_q, Db_qn);
  and C_prime_D_prime (C_prime_D_prime_out, Dc_qn, Dd_qn);
  and AB_prime_C_prime (AB_prime_C_prime_out, Da_q, Db_qn, Dc_qn);
  and ABCD_prime (ABCD_prime_out, Da_q, Db_q, Dc_q, Dd_qn);
  or a (a_out, AC_prime_out, CD_out, A_prime_BC_out, B_prime_C_prime_D_out);
  or b (b_out, Dd_q, AB_prime_out, AC_prime_out);
  or c (c_out, C_prime_D_prime_out, AB_prime_out);
  or d (d_out, AB_prime_C_prime_out, ABCD_prime_out);
  Clock clock (.out(clock_out));
  D_Flip_Flop Da (.clk(clock_out), .D(a_out), .Q(Da_q), .Qn(Da_qn));  // open: preset, en, reset
  D_Flip_Flop Db (.clk(clock_out), .D(b_out), .Q(Db_q), .Qn(Db_qn));  // open: preset, en, reset
  D_Flip_Flop Dc (.clk(clock_out), .D(c_out), .Q(Dc_q), .Qn(Dc_qn));  // open: preset, en, reset
  D_Flip_Flop Dd (.clk(clock_out), .D(d_out), .Q(Dd_q), .Qn(Dd_qn));  // open: preset, en, reset
  _4x7_Decoder u_4x7_decoder_1 (
    .A(Da_q), .B(Db_q), .C(Dc_q), .D(Dd_q), .out_5(n4x7_decoder_1_out_5), .out_6(n4x7_decoder_1_out_6),
    .out_7(n4x7_decoder_1_out_7), .out_8(n4x7_decoder_1_out_8), .out_9(n4x7_decoder_1_out_9),
    .out_10(n4x7_decoder_1_out_10), .out_11(n4x7_decoder_1_out_11));
  _7_Segment_Display u_7_segment_display_1 (
    .g(n4x7_decoder_1_out_11), .f(n4x7_decoder_1_out_10), .a(n4x7_decoder_1_out_5), .b(n4x7_decoder_1_out_6),
    .e(n4x7_decoder_1_out_9), .d(n4x7_decoder_1_out_8), .c(n4x7_decoder_1_out_7), .dp(1'b0));

  // Notes on the sheet:
  //   Main Circuit
endmodule
